# Fritzing sketch Arduino+Shield (saved by Fritzing 0.9.3b)

parts:
  Componente3 = Base Shield V2
  Composant1 = Arduino Uno (Rev3)

nets:
  N1: Componente3.A0, Composant1.A0
  N2: Componente3.A1, Composant1.A1
  N3: Componente3.A2, Composant1.A2
  N4: Componente3.A3, Composant1.A3
  N5: Componente3.A4, Composant1.A4/SDA
  N6: Componente3.A5, Composant1.A5/SCL
  N7: Componente3.D8, Composant1.D8
  N8: Componente3.D9, Composant1.D9_PWM
  N9: Componente3.D10, Composant1.D10_PWM/SS
  N10: Componente3.D11, Composant1.D11_PWM/MOSI
  N11: Componente3.D12, Composant1.D12/MISO
  N12: Componente3.D13, Composant1.D13/SCK
  GND: Componente3.GND, Composant1.GND
  N13: Componente3.AREF, Composant1.AREF
  N14: Componente3.D0/RX, Composant1.D0/RX
  N15: Componente3.D1/TX, Composant1.D1/TX
  N16: Componente3.D2, Composant1.D2
  N17: Componente3.D3, Composant1.D3_PWM
  N18: Componente3.D4, Composant1.D4
  N19: Componente3.D5, Composant1.D5_PWM
  N20: Componente3.D6_PWM, Composant1.D6_PWM
  N21: Componente3.D7, Composant1.D7
  N22: Componente3.ioref, Composant1.ioref
  N23: Componente3.RESET, Composant1.RESET
  3V3: Componente3.3V3, Composant1.3V3
  5V: Componente3.5V, Composant1.5V
  VIN: Componente3.VIN, Composant1.VIN
  N24: Componente3.N/C, Composant1.N/C
