# Fritzing sketch Shield+DHT11 (saved by Fritzing 0.9.3b)

parts:
  Componente6 = Base Shield V2
  DHT1 = Humidity and Temperature Sensor DHT11

nets:
  N1: Componente6.D5, DHT1.Data-signal
  5V: Componente6.5V, DHT1.Vcc
  N2: Componente6.GND, DHT1.GND_2

custom parts:
  Humidity and Temperature Sensor DHT11: Digital relative humidity & temperature sensor DHT11
