# Fritzing sketch Shield+PmodISNS20 (saved by Fritzing 0.9.3b)

parts:
  Componente4 = Base Shield V2
  PMOD2 = Pmod ISNS20

nets:
  N1: Componente4.D10, PMOD2.CS
  N2: Componente4.D12, PMOD2.DO
  N3: Componente4.D13, PMOD2.CLK
  3V3: Componente4.3V3, PMOD2.VCC
  GND: Componente4.GND, PMOD2.GND

custom parts:
  Pmod ISNS20: The Digilent Pmod ISNS20 (Revision A) is a small current sense module with a digital SPI interface. The board combines an Allegro ACS722 Hall Effect current sensor with a 12-bit analog-to-digital converter from Texas Instruments. The Pmod ISNS20 is quick, accurate, and easy to use for a variety of applications.
