# Fritzing sketch Shield+lcdI2C (saved by Fritzing 0.9.3b)

parts:
  Componente4 = Base Shield V2
  Composant1 = LCD1602-I2C

nets:
  N1: Componente4.pin_124, Composant1.GND
  N2: Componente4.pin_125, Composant1.VCC
  N3: Componente4.pin_126, Composant1.SDA
  N4: Componente4.pin_127, Composant1.SCL

custom parts:
  LCD1602-I2C: A standard character display, usually with 2x16 characters. Comes in many colors with LCM1602 IIC attached.

// code stored in the sketch: affichage.ino
#include <Wire.h>
#include "rgb_lcd.h"

rgb_lcd lcd;
int Tension = A0;
int In=12;
int Courant= 6;

void setup() {

lcd.begin(16,2);

}

void loop() {

 aff_I(In,Courant);
 delay(1000);
}


void aff_I(int tension, int courant){
lcd.clear();
lcd.setCursor(0,0);
lcd.print("Vpv:");
lcd.setCursor(4,0);
lcd.print(tension*4.8);
lcd.setCursor(0,1);
lcd.print("Ipv:");
lcd.setCursor(4,1);
lcd.print(courant);
Serial.println("test sur fritzing");
}
