# Fritzing sketch Tension PV A0 (saved by Fritzing 0.9.3b)
breadboards: 1

parts:
  Componente5 = Base Shield V2
  R1 = Resistor [tolerance=±5% resistance=22k package=THT]  # not connected
  R2 = Resistor [tolerance=±5% resistance=12k package=THT]
  R3 = Resistor [tolerance=±5% resistance=10k package=THT]
  Composant2 = LCD1602-I2C

nets:
  N1: Componente5.A0, R2.Pin_0, R3.Pin_1
  N2: Componente5.GND, R3.Pin_0
  N3: Componente5.pin_124, Composant2.GND
  N4: Componente5.pin_125, Composant2.VCC
  N5: Componente5.pin_126, Composant2.SDA
  N6: Componente5.pin_127, Composant2.SCL

notes:
  +Pv
  -Pv

custom parts:
  LCD1602-I2C: A standard character display, usually with 2x16 characters. Comes in many colors with LCM1602 IIC attached.
