# Fritzing sketch potentiometre + afficheur (saved by Fritzing 0.9.3b)

parts:
  R1 = Rotary Potentiometer (Small) [maximum_resistance=100kΩ package=THT]
  Componente7 = Base Shield V2
  Composant3 = LCD1602-I2C

nets:
  N1: R1.leg1, Componente7.GND
  N2: R1.wiper, Componente7.A0
  N3: R1.leg2, Componente7.5V
  N4: Componente7.pin_124, Composant3.GND
  N5: Componente7.pin_125, Composant3.VCC
  N6: Componente7.pin_126, Composant3.SDA
  N7: Componente7.pin_127, Composant3.SCL

custom parts:
  LCD1602-I2C: A standard character display, usually with 2x16 characters. Comes in many colors with LCM1602 IIC attached.
