# Fritzing sketch shield+AOP+pont+LCD+CS (saved by Fritzing 0.9.3b)
breadboards: 1

parts:
  LM1 = LM741 [part_number=LM741 package="DIP (Dual Inline) [THT]"]
  Componente5 = Base Shield V2
  R1 = Resistor [tolerance=±5% resistance=10k package=THT]
  R2 = Resistor [tolerance=±5% resistance=10k package=THT]
  R4 = Resistor [tolerance=±5% resistance=10k package=THT]
  R5 = Resistor [tolerance=±5% resistance=12k package=THT]
  R6 = Resistor [tolerance=±5% resistance=22k package=THT]
  PMOD3 = Pmod ISNS20

nets:
  N1: LM1.pin2, R1.Pin_0, R2.Pin_1
  N2: LM1.pin3, Componente5.D3
  N3: LM1.pin6, R1.Pin_1
  N4: Componente5.A0, R4.Pin_0, R5.Pin_1
  N5: Componente5.D10, PMOD3.CS
  N6: Componente5.D12, PMOD3.DO
  N7: Componente5.D13, PMOD3.CLK
  GND: Componente5.GND, R2.Pin_0, R4.Pin_1, PMOD3.GND
  5V: Componente5.5V, PMOD3.VCC
  N8: R5.Pin_0, R6.Pin_1
  N9: R6.Pin_0, PMOD3.IP-

custom parts:
  LM741: This is a single Op Amp DIP.
  Pmod ISNS20: The Digilent Pmod ISNS20 (Revision A) is a small current sense module with a digital SPI interface. The board combines an Allegro ACS722 Hall Effect current sensor with a 12-bit analog-to-digital converter from Texas Instruments. The Pmod ISNS20 is quick, accurate, and easy to use for a variety of applications.
