# Fritzing sketch shield+AOP (saved by Fritzing 0.9.3b)
breadboards: 1

parts:
  LM1 = LM741 [part_number=LM741 package="DIP (Dual Inline) [THT]"]
  Componente5 = Base Shield V2
  R1 = Resistor [tolerance=±5% resistance=220 package=THT]
  R2 = Resistor [tolerance=±5% resistance=220 package=THT]

nets:
  N1: LM1.pin2, R1.Pin_0, R2.Pin_1
  N2: LM1.pin3, Componente5.D3
  N3: LM1.pin6, R1.Pin_1
  N4: Componente5.GND, R2.Pin_0

custom parts:
  LM741: This is a single Op Amp DIP.
